// Logisim project tictactoe_pitic.circ as structural Verilog: 4 circuits, main circuit main
module main (
);

  wire B1, B2, B3, B4, B5, B6, B7, B8, B9, or_1_out, reset, win_logic_1_win_o, win_logic_1_win_x;
  wire [1:0] C1, C2, C3, C4, C5, C6, C7, C8, C9, S;

  Button button_1 (.out(B1));
  Button button_2 (.out(B4));
  Button button_3 (.out(B7));
  or or_1 (or_1_out, B1, B2, B3, B4, B5, B6, B7, B8, B9);
  Celula celula_1 (.in_1(S), .in_2(B1), .in_3(reset), .out_4(C1));
  Celula celula_2 (.in_1(S), .in_2(B4), .in_3(reset), .out_4(C4));
  Celula celula_3 (.in_1(S), .in_2(B7), .in_3(reset), .out_4(C7));
  Button u_reset (.out(reset));
  // RGBLED rgbled_1: pin names not known; wires that end beside it: C1[0]
  // RGBLED rgbled_2: pin names not known; wires that end beside it: C1[1]
  // RGBLED rgbled_3: pin names not known; wires that end beside it: C4[0]
  // RGBLED rgbled_4: pin names not known; wires that end beside it: C4[1]
  // RGBLED rgbled_5: pin names not known; wires that end beside it: C7[0]
  // RGBLED rgbled_6: pin names not known; wires that end beside it: C7[1]
  Button button_4 (.out(B2));
  Button button_5 (.out(B5));
  Button button_6 (.out(B8));
  Schimbare_Jucator schimbare_jucator_1 (.in_1(or_1_out), .out_2(S));
  // RGBLED rgbled_7: pin names not known; wires that end beside it: C2[0]
  Celula celula_4 (.in_1(S), .in_2(B2), .in_3(reset), .out_4(C2));
  // RGBLED rgbled_8: pin names not known; wires that end beside it: C2[1], reset
  // RGBLED rgbled_9: pin names not known; wires that end beside it: C5[0]
  Celula celula_5 (.in_1(S), .in_2(B5), .in_3(reset), .out_4(C5));
  // RGBLED rgbled_10: pin names not known; wires that end beside it: C5[1]
  // RGBLED rgbled_11: pin names not known; wires that end beside it: C8[0]
  Celula celula_6 (.in_1(S), .in_2(B8), .in_3(reset), .out_4(C8));
  // RGBLED rgbled_12: pin names not known; wires that end beside it: C8[1]
  Button button_7 (.out(B3));
  Button button_8 (.out(B6));
  Button button_9 (.out(B9));
  Win_Logic win_logic_1 (
    .C1(C1), .C2(C2), .C3(C3), .C4(C4), .C5(C5), .C6(C6), .C7(C7), .C8(C8), .C9(C9),
    .WIN_x(win_logic_1_win_x), .WIN_o(win_logic_1_win_o));
  // RGBLED rgbled_13: pin names not known; wires that end beside it: win_logic_1_win_x
  // RGBLED rgbled_14: pin names not known; wires that end beside it: win_logic_1_win_o
  // RGBLED rgbled_15: pin names not known; wires that end beside it: C3[0]
  Celula celula_7 (.in_1(S), .in_2(B3), .in_3(reset), .out_4(C3));
  // RGBLED rgbled_16: pin names not known; wires that end beside it: C3[1]
  // RGBLED rgbled_17: pin names not known; wires that end beside it: C6[0]
  Celula celula_8 (.in_1(S), .in_2(B6), .in_3(reset), .out_4(C6));
  // RGBLED rgbled_18: pin names not known; wires that end beside it: C6[1]
  // RGBLED rgbled_19: pin names not known; wires that end beside it: C9[0]
  Celula celula_9 (.in_1(S), .in_2(B9), .in_3(reset), .out_4(C9));
  // RGBLED rgbled_20: pin names not known; wires that end beside it: C9[1]
endmodule

module Celula (
  input  [1:0] in_1,
  input  in_2,
  input  in_3,
  output [1:0] out_4
);

  wire nor_1_out;

  Register #(.width(2)) register_1 (.D(in_1), .en(nor_1_out), .clk(in_2), .Q(out_4), .clr(in_3));
  nor nor_1 (nor_1_out, out_4[0], out_4[1]);
endmodule

module Schimbare_Jucator (
  input  in_1,
  output [1:0] out_2
);

  wire t_ff_1_q;

  T_Flip_Flop t_ff_1 (.T(1'b1), .clk(in_1), .Q(t_ff_1_q));  // open: Qn, reset, preset
  Multiplexer #(.width(2)) multiplexer_1 (.in0(2'b01), .in1(2'b10), .out(out_2), .sel(t_ff_1_q));
endmodule

module Win_Logic (
  input  [1:0] C1,
  input  [1:0] C2,
  input  [1:0] C3,
  input  [1:0] C4,
  input  [1:0] C5,
  input  [1:0] C6,
  input  [1:0] C7,
  input  [1:0] C8,
  input  [1:0] C9,
  output WIN_x,
  output WIN_o
);

  wire and_1_out, and_2_out, and_3_out, and_4_out, and_5_out, and_6_out, and_7_out, and_8_out, and_9_out,
       and_10_out, and_11_out, and_12_out, and_13_out, and_14_out, and_15_out, and_16_out;

  and and_1 (and_1_out, C1[0], C2[0], C3[0]);
  and and_2 (and_2_out, C4[0], C5[0], C6[0]);
  and and_3 (and_3_out, C7[0], C8[0], C9[0]);
  and and_4 (and_4_out, C1[0], C4[0], C7[0]);
  and and_5 (and_5_out, C2[0], C5[0], C8[0]);
  and and_6 (and_6_out, C3[0], C6[0], C9[0]);
  and and_7 (and_7_out, C1[0], C5[0], C9[0]);
  and and_8 (and_8_out, C3[0], C5[0], C7[0]);
  or or_1 (WIN_x, and_1_out, and_2_out, and_3_out, and_4_out, and_5_out, and_6_out, and_7_out, and_8_out);
  and and_9 (and_9_out, C1[1], C2[1], C3[1]);
  and and_10 (and_10_out, C4[1], C5[1], C6[1]);
  and and_11 (and_11_out, C7[1], C8[1], C9[1]);
  and and_12 (and_12_out, C1[1], C4[1], C7[1]);
  and and_13 (and_13_out, C2[1], C5[1], C8[1]);
  and and_14 (and_14_out, C3[1], C6[1], C9[1]);
  and and_15 (and_15_out, C1[1], C5[1], C9[1]);
  and and_16 (and_16_out, C3[1], C5[1], C7[1]);
  or or_2 (WIN_o, and_9_out, and_10_out, and_11_out, and_12_out, and_13_out, and_14_out, and_15_out, and_16_out);

  // Other names for the same wires on the sheet: C1_0 = C1[0]; C1_X = C1[1]; C2_0 = C2[0]; C2_X = C2[1]; C3_0 = C3[0];
  //   C3_X = C3[1]; C4_0 = C4[0]; C4_X = C4[1]; C5_0 = C5[0]; C5_X = C5[1]; C6_0 = C6[0]; C6_X = C6[1]; C7_0 = C7[0];
  //   C7_X = C7[1]; C8_0 = C8[0]; C8_X = C8[1]; C9_0 = C9[0]; C9_X = C9[1]
endmodule
